# Fritzing sketch AutoWateringSystem (saved by Fritzing 0.9.3b)
breadboards: 1

parts:
  Part1 = Arduino Uno (Rev3)
  Part2 = FC-28 Soil Hygrometer Module - Probe
  Part3 = FC-28 Soil Hygrometer Module
  Part4 = FC-28 Soil Hygrometer Module
  Part5 = FC-28 Soil Hygrometer Module - Probe
  8x8_LED_Modul_mit_MAX1 = 8x8 LED Modul mit MAX7219 [package=THT]
  Part6 = Bluetooth HC-05 Macho
  S1 = H-Bridge with L298N
  M1 = DC Motor
  LED1 = RGB LED - (4 legs) [package="5 mm [THT]"]

nets:
  N1: Part1.A0, Part3.AO
  N2: Part1.A1, Part4.AO
  N3: Part1.D9_PWM, LED1.common_anode
  N4: Part1.D10_PWM/SS, S1.IN4
  N5: Part1.D11_PWM/MOSI, LED1.red_cathode
  N6: Part1.D0/RX, Part6.TXD
  N7: Part1.D1/TX, Part6.RXD
  N8: Part1.D3_PWM, LED1.green_cathode
  N9: Part1.D5_PWM, 8x8_LED_Modul_mit_MAX1.CLK_Eingang
  N10: Part1.D6_PWM, 8x8_LED_Modul_mit_MAX1.CS_Eingang
  N11: Part1.D7, 8x8_LED_Modul_mit_MAX1.DIN_Eingang
  VCC: Part1.5V, Part3.VCC, Part4.VCC, 8x8_LED_Modul_mit_MAX1.VCC_Eingang, Part6.VCC, S1.12V
  GND: Part1.GND, Part3.GND, Part4.GND, 8x8_LED_Modul_mit_MAX1.GND_Eingang, Part6.GND, S1.GND, LED1.blue_cathode
  N12: Part2.POS, Part3.POS
  N13: Part2.NEG, Part3.NEG
  N14: Part4.POS, Part5.POS
  N15: Part4.NEG, Part5.NEG
  N16: S1.M2-01, M1.pin_2
  N17: S1.M2-02, M1.pin_1

custom parts:
  FC-28 Soil Hygrometer Module - Probe: The FC-28 is a soil hygrometer module that uses the Texas Instruments LM393 comparator chip to provide an analog measurement of soil humidity.
  FC-28 Soil Hygrometer Module: The FC-28 is a soil hygrometer module that uses the Texas Instruments LM393 comparator chip to provide an analog measurement of soil humidity. The digital output is high when soil moisture is over a certain threshold, as determined by adjusting the potentiometer.
  H-Bridge with L298N: h-bridge
